# Fritzing sketch StratoBalloon (saved by Fritzing 0.9.3b)
breadboards: 1
perfboards: 1

parts:
  Grove1 = Grove OLED 128x96
  Raspberry_Pi_Zero1 = Raspberry Pi Zero  # not connected
  S1 = Round Pushbutton  # not connected
  U1 = TEMPERATURE-SENSOR [package=to-92]  # not connected
  R1 = Resistor [tolerance=±5% resistance=220 package=THT]
  S2 = Pushbutton [package="[THT]"]
  R2 = Resistor [tolerance=±5% resistance=220 package=THT]  # not connected
  RHT1 = Humidity and Temperature Sensor RHT03
  VCC1 = Battery  # not connected
  J1 = shrouded pin header, 40 pins [form="♂ (shrouded male)"]
  LED1 = LED - 3mm [color="Red (633nm)" package="3 mm [THT]"]  # not connected
  LED2 = LED - 3mm [color="Red (633nm)" package="3 mm [THT]"]  # not connected
  R3 = Resistor [tolerance=±5% resistance=220 package=THT]

nets:
  N1: Grove1.GND, RHT1.GND_2, J1.pin5
  VCC: Grove1.VCC, RHT1.Vcc, J1.pin1, R3.Pin_1
  N2: Grove1.SDA, J1.pin2
  N3: Grove1.SCL, J1.pin3
  N4: R1.Pin_0, J1.pin25
  N5: R1.Pin_1, J1.pin29
  N6: S2.Pin_1, S2.Pin_2
  N7: S2.Pin_3, S2.Pin_4
  N8: RHT1.Data-signal, J1.pin4, R3.Pin_0
